# Fritzing sketch potentiometer (saved by Fritzing 0.9.2b)
breadboards: 1

parts:
  Pro_Micro1 = Pro Micro  # not connected
  LED1 = LED - 5mm [color="Red (633nm)" package="5 mm [THT]"]
  R1 = Rotary Potentiometer (Small) [maximum_resistance=100kΩ package=THT]

nets:
  N1: LED1.anode, R1.leg2

custom parts:
  Pro Micro: The SparkFun Pro Micro is a complete USB-based microcontoller development system, in a very small footprint, capable of implementing many types of projects. All programming can be done via the USB port.
